# Fritzing sketch valve-controller (saved by Fritzing 0.9.10b)
circuit board: 7.9569cm x 6.39254cm
perfboards: 1

parts:
  Part1 = Arduino Nano (Rev3.0)
  J1 = female pin header, 15 pins [form="♀ (female)"]
  LED1 = LED - 5mm [color="Orange (620nm)" current=0.030 package="5 mm [THT]"]
  LED2 = LED - 5mm [color="Orange (620nm)" current=0.030 package="5 mm [THT]"]
  LED3 = LED - 5mm [color="Orange (620nm)" current=30mA package="5 mm [THT]"]
  LED4 = LED - 5mm [color="Orange (620nm)" current=0.030 package="5 mm [THT]"]
  LED5 = LED - 5mm [color="Orange (620nm)" current=0.030 package="5 mm [THT]"]
  R2 = Resistor [tolerance=±5% power=0.25 resistance=220 package=THT]
  R4 = Resistor [tolerance=±5% power=0.25 resistance=220 package=THT]
  R5 = Resistor [tolerance=±5% power=0.25 resistance=220 package=THT]
  Q1 = Basic FET N-Channel [package="TO220 [THT]"]
  Q2 = Basic FET N-Channel [package="TO220 [THT]"]
  Q3 = Basic FET N-Channel [package="TO220 [THT]"]
  Q4 = Basic FET N-Channel [package="TO220 [THT]"]
  Q5 = Basic FET N-Channel [package="TO220 [THT]"]
  J1_2 = Camdenboss CTB0158-2 [part_number=CTB0158-2 package=THT]  # not connected
  R3 = Resistor [tolerance=±5% power=0.25 resistance=220 package=THT]
  R1 = Resistor [tolerance=±5% power=0.25 resistance=220 package=THT]
  J3 = Camdenboss CTB0158-3 [part_number=CTB0158-3 package=THT]  # not connected
  J2 = Camdenboss CTB0158-2 [part_number=CTB0158-2 package=THT]  # not connected
  J2_2 = female pin header, 15 pins [form="♀ (female)"]

nets:
  N1: Part1.GND, J1.pin14, J2_2.pin12
  N2: Part1.D2, Q1.gate, R1.Pin_0, J2_2.pin11
  N3: Part1.D3, R2.Pin_1, Q2.gate, J2_2.pin10
  N4: Part1.D4, Q3.gate, R3.Pin_1, J2_2.pin9
  N5: Part1.D5, R4.Pin_0, Q4.gate, J2_2.pin8
  N6: Part1.D6, R5.Pin_0, Q5.gate, J2_2.pin7
  N7: Part1.VIN, J1.pin15
  N8: LED1.anode, R1.Pin_1
  N9: LED2.anode, R2.Pin_0
  N10: LED3.anode, R3.Pin_0
  N11: LED4.anode, R4.Pin_1
  N12: LED5.anode, R5.Pin_1
